// Digital circuit Bit.dig as structural Verilog
module Bit (
  input  in,
  input  load,
  input  \time ,
  output out
);

  wire mux_1_out;

  Mux mux_1 (.a(out), .b(in), .sel(load), .out(mux_1_out));
  DFF dff_1 (.data(mux_1_out), .\time (\time ), .out(out));
endmodule

/* Test case:
  time   in   load   out  

while(out)
   C      0     1     x   
end while

   1      0     0     0   
   0      0     0     0   
   1      0     1     0   
   0      0     1     0   
   1      1     0     0   
   0      1     0     0   
   1      1     1     0   
   0      1     1     1   
   1      0     0     1   
   0      0     0     1   
   1      1     0     1   
   0      1     0     1   
   1      0     1     1   
   0      0     1     0   
   1      1     1     0   
   0      1     1     1   
   1      0     0     1   
   0      0     0     1   
   1      0     0     1   
   0      0     0     1   
   1      0     0     1   
   0      0     0     1   
   1      0     0     1   
   0      0     0     1   
   1      0     0     1   
   0      0     0     1   
   1      0     0     1   
   0      0     0     1   
   1      0     0     1   
   0      0     0     1   
   1      0     0     1   
   0      0     0     1   
   1      0     0     1   
   0      0     0     1   
   1      0     0     1   
   0      0     0     1   
   1      0     0     1   
   0      0     0     1   
   1      0     0     1   
   0      0     0     1   
   1      0     0     1   
   0      0     0     1   
   1      0     0     1   
   0      0     0     1   
   1      0     0     1   
   0      0     0     1   
   1      0     0     1   
   0      0     0     1   
   1      0     0     1   
   0      0     0     1   
   1      0     0     1   
   0      0     0     1   
   1      0     0     1   
   0      0     0     1   
   1      0     0     1   
   0      0     0     1   
   1      0     0     1   
   0      0     0     1   
   1      0     0     1   
   0      0     0     1   
   1      0     0     1   
   0      0     0     1   
   1      0     0     1   
   0      0     0     1   
   1      0     0     1   
   0      0     0     1   
   1      0     0     1   
   0      0     0     1   
   1      0     0     1   
   0      0     0     1   
   1      0     0     1   
   0      0     0     1   
   1      0     0     1   
   0      0     0     1   
   1      0     0     1   
   0      0     0     1   
   1      0     0     1   
   0      0     0     1   
   1      0     0     1   
   0      0     0     1   
   1      0     0     1   
   0      0     0     1   
   1      0     0     1   
   0      0     0     1   
   1      0     0     1   
   0      0     0     1   
   1      0     0     1   
   0      0     0     1   
   1      0     0     1   
   0      0     0     1   
   1      0     0     1   
   0      0     0     1   
   1      0     0     1   
   0      0     0     1   
   1      0     0     1   
   0      0     0     1   
   1      0     0     1   
   0      0     0     1   
   1      0     0     1   
   0      0     0     1   
   1      0     0     1   
   0      0     0     1   
   1      0     0     1   
   0      0     0     1   
   1      0     0     1   
   0      0     0     1   
   1      0     0     1   
   0      0     0     1   
   1      0     0     1   
   0      0     0     1   
   1      0     0     1   
   0      0     0     1   
   1      0     0     1   
   0      0     0     1   
   1      0     1     1   
   0      0     1     0   
   1      1     0     0   
   0      1     0     0   
   1      1     0     0   
   0      1     0     0   
   1      1     0     0   
   0      1     0     0   
   1      1     0     0   
   0      1     0     0   
   1      1     0     0   
   0      1     0     0   
   1      1     0     0   
   0      1     0     0   
   1      1     0     0   
   0      1     0     0   
   1      1     0     0   
   0      1     0     0   
   1      1     0     0   
   0      1     0     0   
   1      1     0     0   
   0      1     0     0   
   1      1     0     0   
   0      1     0     0   
   1      1     0     0   
   0      1     0     0   
   1      1     0     0   
   0      1     0     0   
   1      1     0     0   
   0      1     0     0   
   1      1     0     0   
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*/
